// Logisim project common_bus.circ as structural Verilog: 1 circuit, main circuit main
module main (
  input  [1:0] in_1,
  input  [3:0] in_2,
  input  [3:0] in_3,
  input  [3:0] in_4,
  input  [3:0] in_5,
  output [3:0] out_6
);

  wire clock_1_out;
  wire [3:0] A_q, B_q, C_q, D_q;

  Multiplexer #(.select(2)) multiplexer_1 (
    .in0(A_q[0]), .in1(B_q[0]), .in2(C_q[0]), .in3(D_q[0]), .out(out_6[0]), .sel(in_1));
  Register #(.width(4)) A (.D(in_2), .clk(clock_1_out), .Q(A_q));  // open: en, clr
  Clock clock_1 (.out(clock_1_out));
  Multiplexer #(.select(2)) multiplexer_2 (
    .in0(A_q[1]), .in1(B_q[1]), .in2(C_q[1]), .in3(D_q[1]), .out(out_6[1]), .sel(in_1));
  Register #(.width(4)) B (.D(in_3), .clk(clock_1_out), .Q(B_q));  // open: en, clr
  Register #(.width(4)) C (.D(in_4), .clk(clock_1_out), .Q(C_q));  // open: en, clr
  Multiplexer #(.select(2)) multiplexer_3 (
    .in0(A_q[2]), .in1(B_q[2]), .in2(C_q[2]), .in3(D_q[2]), .out(out_6[2]), .sel(in_1));
  Register #(.width(4)) D (.D(in_5), .clk(clock_1_out), .Q(D_q));  // open: en, clr
  Multiplexer #(.select(2)) multiplexer_4 (
    .in0(A_q[3]), .in1(B_q[3]), .in2(C_q[3]), .in3(D_q[3]), .out(out_6[3]), .sel(in_1));
endmodule
